// Logisim project LabArqui.circ as structural Verilog
module OneBitComparer (
  input  A,
  input  B,
  output AGB,
  output ALB,
  output AEB
);

  wire not_1_out, not_2_out, or_1_out;

  not not_1 (not_1_out, B);
  not not_2 (not_2_out, A);
  and and_1 (AGB, A, not_1_out);
  buf and_2 (ALB, not_2_out);  // AND_Gate
  or or_1 (or_1_out, AGB, ALB);
  not not_3 (AEB, or_1_out);

  // Notes on the sheet:
  //   A>B
  //   A<B
  //   A=B
endmodule

module EightBitComparer (
  input  in_1,
  input  in_2
);

  OneBitComparer onebitcomparer_1 (.A(in_1), .B(in_2));  // open: AGB, ALB, AEB
endmodule

module TwoBitsComparer (
  input  A0,
  input  A1,
  input  B0,
  input  B1,
  output out_5
);

  wire onebitcomparer_1_aeb, onebitcomparer_2_aeb;

  OneBitComparer onebitcomparer_1 (.A(A0), .B(B0), .AEB(onebitcomparer_1_aeb));  // open: AGB, ALB
  OneBitComparer onebitcomparer_2 (.A(A1), .B(B1), .AEB(onebitcomparer_2_aeb));  // open: AGB, ALB
  and and_1 (out_5, onebitcomparer_1_aeb, onebitcomparer_2_aeb);
endmodule
